# Fritzing sketch StepperController (saved by Fritzing 0.3.19b)
breadboards: 1

parts:
  LD293D = H-Bridge [package=THT]
  BIPOLAR_STEPPER = Stepper Motor - Bipolar
  10K0 = Resistor [resistance=10k package=THT]
  J1 = female pin header, 4 pins [form="♀ (female)"]
  2N2222 = NPN-Transistor [package="TO92 [THT]"]
  1K0 = Resistor [resistance=1k package=THT]
  10K = Resistor [resistance=10k package=THT]
  1K = Resistor [resistance=1k package=THT]
  2N2222_2 = NPN-Transistor [package="TO92 [THT]"]

nets:
  N1: LD293D.1_2EN, J1.pin3
  N2: LD293D.1A, J1.pin1, 1K0.Pin_0
  N3: LD293D.1Y, BIPOLAR_STEPPER.D
  GND: LD293D.GND1, LD293D.GND2, LD293D.GND3, LD293D.GND4, 2N2222.E, 2N2222_2.E
  N4: LD293D.2Y, BIPOLAR_STEPPER.B
  N5: LD293D.2A, 10K0.Pin_1, 2N2222.C
  12V: LD293D.VCC2
  N6: LD293D.3_4EN, J1.pin4
  N7: LD293D.3A, 10K.Pin_0, 2N2222_2.C
  N8: LD293D.3Y, BIPOLAR_STEPPER.C
  N9: LD293D.4Y, BIPOLAR_STEPPER.A
  N10: LD293D.4A, J1.pin2, 1K.Pin_0
  5V: LD293D.VCC1, 10K0.Pin_0, 10K.Pin_1
  N11: 2N2222.B, 1K0.Pin_1
  N12: 1K.Pin_1, 2N2222_2.B

notes:
  1 - Control A
  2 - Control B
  3 - Enable A (PWM)
  4 - Enable B (PWM)
  Motor Supply 5-30V
