# Fritzing sketch barebones-arduino_Arduino-no-FTDI (saved by Fritzing 0.3.2b)
breadboards: 1

parts:
  C1 = Electrolytic Capacitor [package=THT]
  C2 = Electrolytic Capacitor [package=THT]
  U1 = Voltage Regulator - 5V [package="TO220 [THT]"]
  U2 = atmega168 [package="DIP28 [THT]"]
  R1 = 1k Ω Resistor [package=THT]
  S1 = Pushbutton [package=THT]
  C3 = Ceramic Disk Capacitor [package=THT]
  C4 = Ceramic Disk Capacitor [package=THT]
  XTAL1 = Crystal [package=THT]
  Power_plug1 = Power plug

nets:
  GND: C1.-, C2.-, U1.GND, U2.Pin_8, U2.Pin_22, S1.Pin_3, S1.Pin_4, C3.pin_1, C4.pin_0, Power_plug1.GND
  N1: C1.+, U1.input_voltage, Power_plug1.VCC
  N2: C2.+, U1.output_voltage, U2.Pin_7, U2.Pin_20, U2.Pin_21, R1.Pin_0
  N3: U2.Pin_1, R1.Pin_1, S1.Pin_1, S1.Pin_2
  N4: U2.Pin_9, C4.pin_1, XTAL1.pin_0
  N5: U2.Pin_10, C3.pin_0, XTAL1.pin_1

notes:
  This is a breadboard Arduino without an FTDI chip. You can program the chip with a USB-Serial breakout board, by using an external programmer or by programming the MCU in an Arduino board and then popping it into this circuit. The power source should be at least 7 VDC. Related example: http://itp.nyu.edu/physcomp/Tutorials/ArduinoBreadboard
