# Fritzing sketch layout1_led (saved by Fritzing 0.8.7b)
circuit board: 8.46667cm x 5.64444cm
breadboards: 1

parts:
  Part1 = Arduino Uno (Rev3)
  LED1 = LED - 3mm [color="Red (633nm)" package="3 mm [THT]"]
  LED2 = LED - 3mm [color="Green (570nm)" package="3 mm [THT]"]
  LED3 = LED - 3mm [color="Yellow (595nm)" package="3 mm [THT]"]
  S1 = Pushbutton [package="[THT]"]
  R2 = Resistor [tolerance=±5% resistance=10k package=THT]
  S2 = Pushbutton [package="[THT]"]
  R3 = Resistor [tolerance=±5% resistance=10k package=THT]

nets:
  N1: Part1.D11_PWM/MOSI, LED3.anode
  N2: Part1.D12/MISO, LED1.anode
  N3: Part1.D13/SCK, LED2.anode
  N4: Part1.GND, LED1.cathode, LED2.cathode, LED3.cathode, R2.Pin_1, R3.Pin_0
  N5: Part1.D2, S1.Pin_1, S1.Pin_2, R2.Pin_0
  N6: Part1.D3_PWM, S2.Pin_3, S2.Pin_4, R3.Pin_1
  N7: Part1.5V, S1.Pin_3, S1.Pin_4, S2.Pin_1, S2.Pin_2

notes:
  This is a basic input/output uC feedback setup I use. It is intended to be reused for most of the Decision and Loops examples covered in this "Back to Basics" refresher
  -glennlopez
  buttonA
  buttonB
